# Fritzing sketch lab05wiring (saved by Fritzing 0.9.3b)
breadboards: 1

parts:
  Raspberry_Pi_1 = Raspberry Pi 3 [part_number=RPI-3-V1.2]
  J1 = Basic Servo
  R1 = Resistor [tolerance=±5% resistance=330 package=THT]  # not connected
  S1 = Pushbutton [package="[THT]"]

nets:
  GND: Raspberry_Pi_1.GND, Raspberry_Pi_1.GIPO12, Raspberry_Pi_1.GIPO14, J1.gnd, S1.Pin_1, S1.Pin_2, S1.Pin_3, S1.Pin_4
  5V: Raspberry_Pi_1.5V, J1.vcc
